// Logisim project 2_etapa_SOMADOR_E_SUBTRATOR_Daniel_Ribeiro_de_Brito.circ as structural Verilog: 1 circuit, main circuit main
module main (
  input  A3,
  input  A2,
  input  A1,
  input  A0,
  input  B3,
  input  B2,
  input  B1,
  input  B0,
  input  Modo
);

  wire adder_1_cout, adder_1_out, adder_2_cout, adder_2_out, adder_3_cout, adder_3_out, adder_4_cout,
       adder_4_out, and_1_out, and_2_out, and_3_out, and_4_out, and_5_out, and_6_out, and_7_out, and_8_out,
       and_9_out, and_10_out, and_11_out, and_12_out, and_13_out, and_14_out, and_15_out, and_16_out,
       and_17_out, and_18_out, and_19_out, and_20_out, and_21_out, and_22_out, not_1_out, not_2_out,
       not_3_out, not_4_out, or_1_out, or_2_out, or_3_out, or_4_out, or_5_out, or_6_out, or_7_out, xor_1_out,
       xor_2_out, xor_3_out, xor_4_out;

  xor xor_1 (xor_1_out, B3, Modo);
  xor xor_2 (xor_2_out, B2, Modo);
  xor xor_3 (xor_3_out, B1, Modo);
  xor xor_4 (xor_4_out, B0, Modo);
  LED led_1 (.in(adder_1_cout));
  LED led_2 (.in(adder_1_out));
  Adder #(.width(1)) adder_1 (.a(A3), .b(xor_1_out), .out(adder_1_out), .cin(adder_2_cout), .cout(adder_1_cout));
  LED led_3 (.in(adder_2_out));
  Adder #(.width(1)) adder_2 (.a(A2), .b(xor_2_out), .out(adder_2_out), .cin(adder_3_cout), .cout(adder_2_cout));
  LED led_4 (.in(adder_3_out));
  Adder #(.width(1)) adder_3 (.a(A1), .b(xor_3_out), .out(adder_3_out), .cin(adder_4_cout), .cout(adder_3_cout));
  LED led_5 (.in(adder_4_out));
  Adder #(.width(1)) adder_4 (.a(A0), .b(xor_4_out), .out(adder_4_out), .cin(Modo), .cout(adder_4_cout));
  not not_1 (not_1_out, adder_1_out);
  not not_2 (not_2_out, adder_2_out);
  not not_3 (not_3_out, adder_3_out);
  not not_4 (not_4_out, adder_4_out);
  and and_1 (and_1_out, not_1_out, adder_3_out);
  and and_2 (and_2_out, not_3_out, adder_1_out, adder_4_out);
  and and_3 (and_3_out, not_1_out, adder_2_out, adder_4_out);
  and and_4 (and_4_out, not_2_out, not_3_out, not_4_out);
  and and_5 (and_5_out, not_1_out, not_2_out);
  and and_6 (and_6_out, not_2_out, not_3_out);
  and and_7 (and_7_out, not_3_out, not_4_out);
  and and_8 (and_8_out, not_1_out, adder_4_out, adder_3_out);
  and and_9 (and_9_out, not_1_out, adder_2_out);
  and and_10 (and_10_out, not_2_out, adder_4_out);
  _7_Segment_Display u_7_segment_display_1 (
    .g(or_7_out), .f(or_6_out), .a(or_1_out), .b(or_2_out), .e(or_5_out), .d(or_4_out), .c(or_3_out));  // open: dp
  LED led_6 (.in(or_1_out));
  or or_1 (or_1_out, and_1_out, and_2_out, and_3_out, and_4_out);
  LED led_7 (.in(or_2_out));
  or or_2 (or_2_out, and_5_out, and_6_out, and_7_out, and_8_out);
  LED led_8 (.in(or_3_out));
  or or_3 (or_3_out, and_6_out, and_9_out, and_10_out);
  and and_11 (and_11_out, not_2_out, not_4_out);
  and and_12 (and_12_out, adder_1_out, not_2_out);
  and and_13 (and_13_out, not_4_out, adder_3_out);
  and and_14 (and_14_out, adder_2_out, not_3_out, adder_4_out);
  and and_15 (and_15_out, not_2_out, not_2_out, adder_3_out);
  LED led_9 (.in(or_4_out));
  or or_4 (or_4_out, and_11_out, and_12_out, and_13_out, and_14_out, and_15_out);
  LED led_10 (.in(or_5_out));
  or or_5 (or_5_out, and_11_out, and_13_out);
  and and_16 (and_16_out, adder_1_out, not_3_out);
  and and_17 (and_17_out, adder_2_out, not_3_out);
  and and_18 (and_18_out, adder_2_out, not_4_out);
  and and_19 (and_19_out, not_4_out, not_3_out);
  and and_20 (and_20_out, adder_1_out, not_2_out);
  and and_21 (and_21_out, not_2_out, adder_3_out);
  and and_22 (and_22_out, not_4_out, adder_3_out);
  LED led_11 (.in(or_6_out));
  or or_6 (or_6_out, and_16_out, and_17_out, and_18_out, and_19_out);
  LED led_12 (.in(or_7_out));
  or or_7 (or_7_out, and_17_out, and_20_out, and_21_out, and_22_out);

  // Notes on the sheet:
  //   0-Soma 1-Subtração
  //   Daniel Ribeiro de Brito
  //   Circuito Somador e Subtrator - 16/11/2022
  //   C4
  //   S3
  //   S2
  //   S1
  //   S0
  //   A'
  //   B'
  //   C'
  //   D'
  //   a
  //   b
  //   c
  //   d
  //   e
  //   f
  //   g
endmodule
