// Logisim project 3_etapa_SOMADOR_E_SUBTRATOR+MUX_Daniel_Ribeiro_de_Brito.circ as structural Verilog: 1 circuit, main circuit main
module main (
  input  A3,
  input  A2,
  input  A1,
  input  A0,
  input  in_5,
  input  B3,
  input  B2,
  input  B1,
  input  in_9,
  input  B0,
  input  Modo,
  input  in_12,
  input  in_13,
  input  in_14,
  input  in_15,
  input  A1_2,
  input  A0_2
);

  wire adder_1_cout, adder_1_out, adder_2_cout, adder_2_out, adder_3_cout, adder_3_out, adder_4_cout,
       adder_4_out, adder_5_out, adder_6_cout, adder_6_out, adder_7_cout, adder_7_out, adder_8_cout,
       adder_8_out, and_1_out, and_2_out, and_3_out, and_4_out, and_5_out, and_6_out, and_7_out, and_8_out,
       and_9_out, and_10_out, and_11_out, and_12_out, and_13_out, and_14_out, and_15_out, and_16_out,
       and_17_out, and_18_out, and_19_out, and_20_out, and_21_out, and_22_out, and_23_out, and_24_out,
       and_25_out, and_26_out, and_27_out, and_28_out, and_29_out, and_30_out, and_31_out, and_32_out,
       and_33_out, and_34_out, and_35_out, and_36_out, and_37_out, and_38_out, and_39_out, and_40_out,
       and_41_out, not_1_out, not_2_out, not_3_out, not_4_out, not_5_out, not_6_out, not_7_out, not_8_out,
       not_9_out, not_10_out, not_11_out, not_12_out, not_13_out, not_14_out, not_15_out, not_16_out,
       not_17_out, not_18_out, not_19_out, not_20_out, not_21_out, not_22_out, or_1_out, or_2_out, or_3_out,
       or_4_out, or_5_out, or_6_out, or_7_out, or_8_out, or_9_out, or_10_out, or_11_out, or_12_out,
       or_13_out, xor_1_out, xor_2_out, xor_3_out, xor_4_out, xor_5_out, xor_6_out, xor_7_out, xor_8_out;

  xor xor_1 (xor_1_out, B3, Modo);
  xor xor_2 (xor_2_out, B2, Modo);
  xor xor_3 (xor_3_out, B1, Modo);
  xor xor_4 (xor_4_out, B0, Modo);
  Adder #(.width(1)) adder_1 (.a(A3), .b(xor_1_out), .out(adder_1_out), .cin(adder_2_cout), .cout(adder_1_cout));
  Adder #(.width(1)) adder_2 (.a(A2), .b(xor_2_out), .out(adder_2_out), .cin(adder_3_cout), .cout(adder_2_cout));
  Adder #(.width(1)) adder_3 (.a(A1), .b(xor_3_out), .out(adder_3_out), .cin(adder_4_cout), .cout(adder_3_cout));
  Adder #(.width(1)) adder_4 (.a(A0), .b(xor_4_out), .out(adder_4_out), .cin(Modo), .cout(adder_4_cout));
  LED led_1 (.in(adder_1_out));
  LED led_2 (.in(adder_2_out));
  LED led_3 (.in(adder_3_out));
  LED led_4 (.in(adder_4_out));
  not not_1 (not_1_out, adder_1_cout);
  not not_2 (not_2_out, Modo);
  or or_1 (or_1_out, and_3_out, adder_1_cout);
  and and_1 (and_1_out, not_1_out, Modo);
  or or_2 (or_2_out, adder_2_out, adder_3_out);
  and and_2 (and_2_out, not_2_out, or_1_out);
  and and_3 (and_3_out, adder_1_out, or_2_out);
  xor xor_5 (xor_5_out, and_1_out, adder_1_out);
  xor xor_6 (xor_6_out, adder_2_out, and_1_out);
  xor xor_7 (xor_7_out, and_1_out, adder_3_out);
  xor xor_8 (xor_8_out, and_1_out, adder_4_out);
  Adder #(.width(1)) adder_5 (.a(in_5), .b(xor_5_out), .out(adder_5_out), .cin(adder_6_cout));  // open: cout
  Adder #(.width(1)) adder_6 (.a(and_2_out), .b(xor_6_out), .out(adder_6_out), .cin(adder_7_cout), .cout(adder_6_cout));
  Adder #(.width(1)) adder_7 (.a(and_2_out), .b(xor_7_out), .out(adder_7_out), .cin(adder_8_cout), .cout(adder_7_cout));
  Adder #(.width(1)) adder_8 (.a(in_9), .b(xor_8_out), .out(adder_8_out), .cin(and_1_out), .cout(adder_8_cout));
  not not_3 (not_3_out, A1_2);
  not not_4 (not_4_out, A0_2);
  not not_5 (not_5_out, A1_2);
  not not_6 (not_6_out, A0_2);
  not not_7 (not_7_out, A1_2);
  not not_8 (not_8_out, A0_2);
  not not_9 (not_9_out, A1_2);
  not not_10 (not_10_out, A0_2);
  not not_11 (not_11_out, A1_2);
  not not_12 (not_12_out, A0_2);
  not not_13 (not_13_out, A1_2);
  not not_14 (not_14_out, A0_2);
  not not_15 (not_15_out, A1_2);
  not not_16 (not_16_out, A0_2);
  not not_17 (not_17_out, A1_2);
  not not_18 (not_18_out, A0_2);
  and and_4 (and_4_out, adder_5_out, not_3_out, not_4_out);
  and and_5 (and_5_out, A3, not_5_out, A0_2);
  and and_6 (and_6_out, B3, A1_2, not_6_out);
  and and_7 (and_7_out, in_12, A1_2, A0_2);
  and and_8 (and_8_out, adder_6_out, not_7_out, not_8_out);
  and and_9 (and_9_out, xor_1_out, not_9_out, A0_2);
  and and_10 (and_10_out, B2, A1_2, not_10_out);
  and and_11 (and_11_out, in_13, A1_2, A0_2);
  and and_12 (and_12_out, adder_7_out, not_11_out, not_12_out);
  and and_13 (and_13_out, A2, not_13_out, A0_2);
  and and_14 (and_14_out, B1, A0_2, not_14_out);
  and and_15 (and_15_out, in_14, A1_2, A0_2);
  and and_16 (and_16_out, adder_8_out, not_15_out, not_16_out);
  and and_17 (and_17_out, xor_2_out, not_17_out, A0_2);
  and and_18 (and_18_out, B0, A1_2, not_18_out);
  and and_19 (and_19_out, in_15, A1_2, A0_2);
  LED led_5 (.in(or_3_out));
  or or_3 (or_3_out, and_4_out, and_5_out, and_6_out, and_7_out);
  LED led_6 (.in(or_4_out));
  or or_4 (or_4_out, and_8_out, and_9_out, and_10_out, and_11_out);
  LED led_7 (.in(or_5_out));
  or or_5 (or_5_out, and_12_out, and_13_out, and_14_out, and_15_out);
  LED led_8 (.in(or_6_out));
  or or_6 (or_6_out, and_16_out, and_17_out, and_18_out, and_19_out);
  not not_19 (not_19_out, or_3_out);
  not not_20 (not_20_out, or_4_out);
  not not_21 (not_21_out, or_5_out);
  not not_22 (not_22_out, or_6_out);
  and and_20 (and_20_out, not_19_out, or_5_out);
  and and_21 (and_21_out, not_21_out, or_3_out, or_6_out);
  and and_22 (and_22_out, not_19_out, or_4_out, or_6_out);
  and and_23 (and_23_out, not_20_out, not_21_out, not_22_out);
  and and_24 (and_24_out, not_19_out, not_20_out);
  and and_25 (and_25_out, not_20_out, not_21_out);
  and and_26 (and_26_out, not_21_out, not_22_out);
  and and_27 (and_27_out, not_19_out, or_6_out, or_5_out);
  _7_Segment_Display u_7_segment_display_1 (
    .g(and_1_out), .b(and_2_out), .c(and_2_out), .dp(and_2_out));  // open: f, a, e, d
  and and_28 (and_28_out, not_19_out, or_4_out);
  and and_29 (and_29_out, not_20_out, or_6_out);
  _7_Segment_Display u_7_segment_display_2 (
    .g(or_13_out), .f(or_12_out), .a(or_7_out), .b(or_8_out), .e(or_11_out), .d(or_10_out), .c(or_9_out));  // open: dp
  LED led_9 (.in(or_7_out));
  or or_7 (or_7_out, and_20_out, and_21_out, and_22_out, and_23_out);
  LED led_10 (.in(or_8_out));
  or or_8 (or_8_out, and_24_out, and_25_out, and_26_out, and_27_out);
  LED led_11 (.in(or_9_out));
  or or_9 (or_9_out, and_25_out, and_28_out, and_29_out);
  and and_30 (and_30_out, not_20_out, not_22_out);
  and and_31 (and_31_out, or_3_out, not_20_out);
  and and_32 (and_32_out, not_22_out, or_5_out);
  and and_33 (and_33_out, or_4_out, not_21_out, or_6_out);
  and and_34 (and_34_out, not_20_out, not_20_out, or_5_out);
  LED led_12 (.in(or_10_out));
  or or_10 (or_10_out, and_30_out, and_31_out, and_32_out, and_33_out, and_34_out);
  LED led_13 (.in(or_11_out));
  or or_11 (or_11_out, and_30_out, and_32_out);
  and and_35 (and_35_out, or_3_out, not_21_out);
  and and_36 (and_36_out, or_4_out, not_21_out);
  and and_37 (and_37_out, or_4_out, not_22_out);
  and and_38 (and_38_out, not_22_out, not_21_out);
  and and_39 (and_39_out, or_3_out, not_20_out);
  and and_40 (and_40_out, not_20_out, or_5_out);
  and and_41 (and_41_out, not_22_out, or_5_out);
  LED led_14 (.in(or_12_out));
  or or_12 (or_12_out, and_35_out, and_36_out, and_37_out, and_38_out);
  LED led_15 (.in(or_13_out));
  or or_13 (or_13_out, and_36_out, and_39_out, and_40_out, and_41_out);

  // Notes on the sheet:
  //   0-Soma 1-Subtração
  //   Circuito Somador e Subtrator - 16/11/2022
  //   Daniel Ribeiro de Brito
  //   C4
  //   S3
  //   S2
  //   S1
  //   S0
  //   A'
  //   B'
  //   C'
  //   D'
  //   a
  //   b
  //   c
  //   d
  //   e
  //   f
  //   g
endmodule
