// Logisim project 6_etapa_Projeto_Final_Daniel_Ribeiro_de_Brito.circ as structural Verilog: 1 circuit, main circuit main
module main (
  input  in_1,
  input  in_2,
  input  CLOCK,
  input  Modo,
  input  T___1,
  input  CLR____1_HABILITA,
  input  ENABLE,
  input  in_8,
  input  ENABLE_2,
  input  in_10,
  input  in_11,
  input  in_12,
  input  in_13,
  input  in_14,
  input  CLK,
  input  RESET_1
);

  wire adder_1_cout, adder_1_out, adder_2_cout, adder_2_out, adder_3_cout, adder_3_out, adder_4_cout,
       adder_4_out, adder_5_out, adder_6_cout, adder_6_out, adder_7_cout, adder_7_out, adder_8_cout,
       adder_8_out, and_1_out, and_2_out, and_3_out, and_4_out, and_5_out, and_6_out, and_7_out, and_8_out,
       and_9_out, and_10_out, and_11_out, and_12_out, and_13_out, and_14_out, and_15_out, and_16_out,
       and_17_out, and_18_out, and_19_out, and_20_out, and_21_out, and_22_out, and_23_out, and_24_out,
       and_25_out, and_26_out, and_27_out, and_28_out, and_29_out, and_30_out, and_31_out, and_32_out,
       and_33_out, and_34_out, and_35_out, and_36_out, and_37_out, and_38_out, and_39_out, and_40_out,
       and_41_out, and_42_out, and_43_out, and_44_out, d_ff_1_q, d_ff_2_q, d_ff_3_q, d_ff_4_q, d_ff_5_q,
       d_ff_6_q, d_ff_7_q, d_ff_8_q, j_k_ff_1_q, j_k_ff_1_qn, j_k_ff_2_q, j_k_ff_2_qn, nand_1_out,
       nand_2_out, not_1_out, not_2_out, not_3_out, not_4_out, not_5_out, not_6_out, not_7_out, not_8_out,
       not_9_out, not_10_out, not_11_out, not_12_out, not_13_out, not_14_out, not_15_out, not_16_out,
       not_17_out, not_18_out, not_19_out, not_20_out, not_21_out, not_22_out, not_23_out, not_24_out,
       or_1_out, or_2_out, or_3_out, or_4_out, or_5_out, or_6_out, or_7_out, or_8_out, or_9_out, or_10_out,
       or_11_out, or_12_out, or_13_out, t_ff_1_q, t_ff_2_q, t_ff_2_qn, t_ff_3_q, t_ff_4_q, t_ff_4_qn,
       xor_1_out, xor_2_out, xor_3_out, xor_4_out, xor_5_out, xor_6_out, xor_7_out, xor_8_out;

  nand nand_1 (nand_1_out, CLR____1_HABILITA, nand_2_out);
  nand nand_2 (nand_2_out, t_ff_1_q, t_ff_4_qn, t_ff_2_qn, t_ff_3_q);
  T_Flip_Flop #(.trigger("falling")) t_ff_1 (
    .clk(t_ff_2_q), .T(T___1), .Q(t_ff_1_q), .reset(nand_1_out));  // open: Qn, preset, en
  T_Flip_Flop #(.trigger("falling")) t_ff_2 (
    .clk(t_ff_3_q), .T(T___1), .Q(t_ff_2_q), .Qn(t_ff_2_qn), .reset(nand_1_out));  // open: preset, en
  T_Flip_Flop #(.trigger("falling")) t_ff_3 (
    .clk(t_ff_4_q), .T(T___1), .Q(t_ff_3_q), .reset(nand_1_out));  // open: Qn, preset, en
  T_Flip_Flop #(.trigger("falling")) t_ff_4 (
    .clk(CLOCK), .T(T___1), .Q(t_ff_4_q), .Qn(t_ff_4_qn), .reset(nand_1_out));  // open: preset, en
  LED led_1 (.in(t_ff_1_q));
  LED led_2 (.in(t_ff_2_q));
  LED led_3 (.in(t_ff_3_q));
  LED led_4 (.in(t_ff_4_q));
  not not_1 (not_1_out, j_k_ff_1_q);
  not not_2 (not_2_out, j_k_ff_2_q);
  D_Flip_Flop #(.trigger("falling")) d_ff_1 (
    .clk(not_2_out), .D(t_ff_1_q), .Q(d_ff_1_q), .en(ENABLE));  // open: Qn, preset, reset
  D_Flip_Flop #(.trigger("falling")) d_ff_2 (
    .clk(not_2_out), .D(t_ff_2_q), .Q(d_ff_2_q), .en(ENABLE));  // open: Qn, preset, reset
  D_Flip_Flop #(.trigger("falling")) d_ff_3 (
    .clk(not_2_out), .D(t_ff_3_q), .Q(d_ff_3_q), .en(ENABLE));  // open: Qn, preset, reset
  D_Flip_Flop #(.trigger("falling")) d_ff_4 (
    .clk(not_2_out), .D(t_ff_4_q), .Q(d_ff_4_q), .en(ENABLE));  // open: Qn, preset, reset
  D_Flip_Flop d_ff_5 (.clk(not_1_out), .D(t_ff_1_q), .Q(d_ff_5_q), .en(ENABLE_2));  // open: Qn, preset, reset
  D_Flip_Flop d_ff_6 (.clk(not_1_out), .D(t_ff_2_q), .Q(d_ff_6_q), .en(ENABLE_2));  // open: Qn, preset, reset
  D_Flip_Flop d_ff_7 (.clk(not_1_out), .D(t_ff_3_q), .Q(d_ff_7_q), .en(ENABLE_2));  // open: Qn, preset, reset
  D_Flip_Flop d_ff_8 (.clk(not_1_out), .D(t_ff_4_q), .Q(d_ff_8_q), .en(ENABLE_2));  // open: Qn, preset, reset
  LED led_5 (.in(d_ff_1_q));
  LED led_6 (.in(d_ff_2_q));
  LED led_7 (.in(d_ff_3_q));
  LED led_8 (.in(d_ff_4_q));
  LED led_9 (.in(d_ff_5_q));
  LED led_10 (.in(d_ff_6_q));
  LED led_11 (.in(d_ff_7_q));
  LED led_12 (.in(d_ff_8_q));
  xor xor_1 (xor_1_out, d_ff_5_q, Modo);
  xor xor_2 (xor_2_out, d_ff_6_q, Modo);
  xor xor_3 (xor_3_out, d_ff_7_q, Modo);
  xor xor_4 (xor_4_out, d_ff_8_q, Modo);
  LED led_13 (.in(adder_1_out));
  Adder #(.width(1)) adder_1 (.a(d_ff_1_q), .b(xor_1_out), .out(adder_1_out), .cin(adder_2_cout), .cout(adder_1_cout));
  LED led_14 (.in(adder_2_out));
  Adder #(.width(1)) adder_2 (.a(d_ff_2_q), .b(xor_2_out), .out(adder_2_out), .cin(adder_3_cout), .cout(adder_2_cout));
  LED led_15 (.in(adder_3_out));
  Adder #(.width(1)) adder_3 (.a(d_ff_3_q), .b(xor_3_out), .out(adder_3_out), .cin(adder_4_cout), .cout(adder_3_cout));
  LED led_16 (.in(adder_4_out));
  Adder #(.width(1)) adder_4 (.a(d_ff_4_q), .b(xor_4_out), .out(adder_4_out), .cin(Modo), .cout(adder_4_cout));
  not not_3 (not_3_out, adder_1_cout);
  LED led_17 (.in(j_k_ff_1_q));
  J_K_Flip_Flop #(.trigger("falling")) j_k_ff_1 (
    .J(j_k_ff_2_q), .clk(CLK), .K(in_13), .Q(j_k_ff_1_q), .Qn(j_k_ff_1_qn), .reset(RESET_1));  // open: preset, en
  not not_4 (not_4_out, Modo);
  or or_1 (or_1_out, and_4_out, adder_1_cout);
  and and_1 (and_1_out, not_3_out, Modo);
  LED led_18 (.in(j_k_ff_2_q));
  J_K_Flip_Flop #(.trigger("falling")) j_k_ff_2 (
    .J(j_k_ff_1_qn), .clk(CLK), .K(in_14), .Q(j_k_ff_2_q), .Qn(j_k_ff_2_qn), .reset(RESET_1));  // open: preset, en
  or or_2 (or_2_out, adder_2_out, adder_3_out);
  and and_2 (and_2_out, j_k_ff_2_qn, j_k_ff_1_qn);
  and and_3 (and_3_out, not_4_out, or_1_out);
  and and_4 (and_4_out, adder_1_out, or_2_out);
  xor xor_5 (xor_5_out, and_1_out, adder_1_out);
  xor xor_6 (xor_6_out, adder_2_out, and_1_out);
  xor xor_7 (xor_7_out, and_1_out, adder_3_out);
  xor xor_8 (xor_8_out, and_1_out, adder_4_out);
  Adder #(.width(1)) adder_5 (.a(in_1), .b(xor_5_out), .out(adder_5_out), .cin(adder_6_cout));  // open: cout
  Adder #(.width(1)) adder_6 (.a(and_3_out), .b(xor_6_out), .out(adder_6_out), .cin(adder_7_cout), .cout(adder_6_cout));
  Adder #(.width(1)) adder_7 (.a(and_3_out), .b(xor_7_out), .out(adder_7_out), .cin(adder_8_cout), .cout(adder_7_cout));
  Adder #(.width(1)) adder_8 (.a(in_2), .b(xor_8_out), .out(adder_8_out), .cin(and_1_out), .cout(adder_8_cout));
  not not_5 (not_5_out, j_k_ff_1_q);
  not not_6 (not_6_out, j_k_ff_2_q);
  not not_7 (not_7_out, j_k_ff_1_q);
  not not_8 (not_8_out, j_k_ff_2_q);
  not not_9 (not_9_out, j_k_ff_1_q);
  not not_10 (not_10_out, j_k_ff_2_q);
  not not_11 (not_11_out, j_k_ff_1_q);
  not not_12 (not_12_out, j_k_ff_2_q);
  not not_13 (not_13_out, j_k_ff_1_q);
  not not_14 (not_14_out, j_k_ff_2_q);
  not not_15 (not_15_out, j_k_ff_1_q);
  not not_16 (not_16_out, j_k_ff_2_q);
  not not_17 (not_17_out, j_k_ff_1_q);
  not not_18 (not_18_out, j_k_ff_2_q);
  not not_19 (not_19_out, j_k_ff_1_q);
  not not_20 (not_20_out, j_k_ff_2_q);
  and and_5 (and_5_out, adder_5_out, not_5_out, not_6_out);
  and and_6 (and_6_out, d_ff_1_q, not_7_out, j_k_ff_2_q);
  and and_7 (and_7_out, d_ff_5_q, j_k_ff_1_q, not_8_out);
  and and_8 (and_8_out, in_8, j_k_ff_1_q, j_k_ff_2_q);
  and and_9 (and_9_out, adder_6_out, not_9_out, not_10_out);
  and and_10 (and_10_out, d_ff_2_q, not_11_out, j_k_ff_2_q);
  and and_11 (and_11_out, d_ff_6_q, j_k_ff_1_q, not_12_out);
  and and_12 (and_12_out, in_10, j_k_ff_1_q, j_k_ff_2_q);
  and and_13 (and_13_out, adder_7_out, not_13_out, not_14_out);
  and and_14 (and_14_out, d_ff_3_q, not_15_out, j_k_ff_2_q);
  and and_15 (and_15_out, d_ff_7_q, j_k_ff_2_q, not_16_out);
  and and_16 (and_16_out, in_11, j_k_ff_1_q, j_k_ff_2_q);
  and and_17 (and_17_out, adder_8_out, not_17_out, not_18_out);
  and and_18 (and_18_out, d_ff_4_q, not_19_out, j_k_ff_2_q);
  and and_19 (and_19_out, d_ff_8_q, j_k_ff_1_q, not_20_out);
  and and_20 (and_20_out, in_12, j_k_ff_1_q, j_k_ff_2_q);
  LED led_19 (.in(or_3_out));
  or or_3 (or_3_out, and_5_out, and_6_out, and_7_out, and_8_out);
  LED led_20 (.in(or_4_out));
  or or_4 (or_4_out, and_9_out, and_10_out, and_11_out, and_12_out);
  LED led_21 (.in(or_5_out));
  or or_5 (or_5_out, and_13_out, and_14_out, and_15_out, and_16_out);
  LED led_22 (.in(or_6_out));
  or or_6 (or_6_out, and_17_out, and_18_out, and_19_out, and_20_out);
  not not_21 (not_21_out, or_3_out);
  not not_22 (not_22_out, or_4_out);
  not not_23 (not_23_out, or_5_out);
  not not_24 (not_24_out, or_6_out);
  and and_21 (and_21_out, and_3_out, and_2_out);
  and and_22 (and_22_out, and_2_out, and_1_out);
  and and_23 (and_23_out, not_21_out, or_5_out);
  and and_24 (and_24_out, not_23_out, or_3_out, or_6_out);
  and and_25 (and_25_out, not_21_out, or_4_out, or_6_out);
  and and_26 (and_26_out, not_22_out, not_23_out, not_24_out);
  and and_27 (and_27_out, not_21_out, not_22_out);
  and and_28 (and_28_out, not_22_out, not_23_out);
  and and_29 (and_29_out, not_23_out, not_24_out);
  and and_30 (and_30_out, not_21_out, or_6_out, or_5_out);
  _7_Segment_Display u_7_segment_display_1 (.g(and_22_out), .b(and_21_out), .c(and_21_out));  // open: f, a, e, d, dp
  and and_31 (and_31_out, not_21_out, or_4_out);
  and and_32 (and_32_out, not_22_out, or_6_out);
  _7_Segment_Display u_7_segment_display_2 (
    .g(or_13_out), .f(or_12_out), .a(or_7_out), .b(or_8_out), .e(or_11_out), .d(or_10_out), .c(or_9_out));  // open: dp
  LED led_23 (.in(or_7_out));
  or or_7 (or_7_out, and_23_out, and_24_out, and_25_out, and_26_out);
  LED led_24 (.in(or_8_out));
  or or_8 (or_8_out, and_27_out, and_28_out, and_29_out, and_30_out);
  LED led_25 (.in(or_9_out));
  or or_9 (or_9_out, and_28_out, and_31_out, and_32_out);
  and and_33 (and_33_out, not_22_out, not_24_out);
  and and_34 (and_34_out, or_3_out, not_22_out);
  and and_35 (and_35_out, not_24_out, or_5_out);
  and and_36 (and_36_out, or_4_out, not_23_out, or_6_out);
  and and_37 (and_37_out, not_22_out, not_22_out, or_5_out);
  LED led_26 (.in(or_10_out));
  or or_10 (or_10_out, and_33_out, and_34_out, and_35_out, and_36_out, and_37_out);
  LED led_27 (.in(or_11_out));
  or or_11 (or_11_out, and_33_out, and_35_out);
  and and_38 (and_38_out, or_3_out, not_23_out);
  and and_39 (and_39_out, or_4_out, not_23_out);
  and and_40 (and_40_out, or_4_out, not_24_out);
  and and_41 (and_41_out, not_24_out, not_23_out);
  and and_42 (and_42_out, or_3_out, not_22_out);
  and and_43 (and_43_out, not_22_out, or_5_out);
  and and_44 (and_44_out, not_24_out, or_5_out);
  LED led_28 (.in(or_12_out));
  or or_12 (or_12_out, and_38_out, and_39_out, and_40_out, and_41_out);
  LED led_29 (.in(or_13_out));
  or or_13 (or_13_out, and_39_out, and_42_out, and_43_out, and_44_out);

  // Notes on the sheet:
  //   CLR = 0 REINICIA
  //   Q3
  //   Q2
  //   Q1
  //   Q0
  //   REG A
  //   REG B
  //   0-Soma 1-Subtração
  //   Daniel Ribeiro de Brito
  //   Circuito Somador, mux e contadores- 18/12/2022
  //   C4
  //   S3
  //   S2
  //   S1
  //   S0
  //   Q1
  //   Q0
  //   01 - NUM A
  //   10 - NUM B
  //   00 - RESULTADO DA OPERAÇÃO
  //   A'
  //   B'
  //   C'
  //   D'
  //   a
  //   b
  //   c
  //   d
  //   e
  //   f
  //   g
endmodule
